// Logisim project lab8_starter_circuit.circ as structural Verilog: 1 circuit, main circuit main
module main (
  input  enable_write,
  input  [7:0] \input ,
  input  select,
  output [7:0] register_contents
);

  wire clock_out;
  wire [7:0] adder_1_out, multiplexer_1_out;

  Clock clock (.out(clock_out));
  Multiplexer #(.width(8), .enable("false")) multiplexer_1 (
    .in0(\input ), .in1(adder_1_out), .out(multiplexer_1_out), .sel(select));
  Adder adder_1 (.a(8'h1), .b(register_contents), .out(adder_1_out));  // open: cin, cout
endmodule
